// Logisim project ULA COMPLETO.circ as structural Verilog: 14 circuits, main circuit main
module main (
  input  Load,
  input  R_1____W_0,
  input  [3:0] in_3,
  output Overflow,
  output Zero
);

  wire clock_1_out, clock_2_out, clock_3_out, not_1_out, not_2_out;
  wire [3:0] ac_1_out_3, mux_1_s, PC_q, ram_1_data, ula_1_s;
  wire [7:0] rom_1_data;

  not not_1 (not_1_out, Load);
  Counter #(.width(4), .max('hf)) PC (
    .load(Load), .D(in_3), .count(not_1_out), .Q(PC_q), .clk(clock_1_out));  // open: carry, clr
  Clock clock_1 (.out(clock_1_out));
  ROM #(.addrWidth(4)) rom_1 (.addr(PC_q), .data(rom_1_data));  // open: sel
  Clock clock_2 (.out(clock_2_out));
  MUX mux_1 (.E(rom_1_data[3:0]), .C(rom_1_data[4]), .D(ram_1_data), .S(mux_1_s));
  // Probe on ac_1_out_3
  ULA ula_1 (
    .D(rom_1_data[4]), .B(mux_1_s), .A(ac_1_out_3), .in_4(rom_1_data[7:5]), .zero(Zero), .Overflow(Overflow),
    .S(ula_1_s));
  // Probe on ula_1_s
  AC ac_1 (.Clock(clock_2_out), .E(ula_1_s), .out_3(ac_1_out_3));
  // Probe on ram_1_data
  // Probe on mux_1_s
  Clock clock_3 (.out(clock_3_out));
  RAM #(.addrWidth(4), .dataWidth(4)) ram_1 (
    .addr(rom_1_data[3:0]), .data(ram_1_data), .clk(clock_3_out), .ld(R_1____W_0));  // open: sel, clr
  not not_2 (not_2_out, R_1____W_0);
  Buffer buffer_1 (.E(ac_1_out_3), .in_2(not_2_out), .S(ram_1_data));

  // Notes on the sheet:
  //   MOV
  //   0
  //   1
  //   MOV
  //   2
  //   ADD
  //   3
  //   ADD
  //   SUB
  //   4
  //   SUB
  //   5
  //   6
  //   OR
  //   OR
  //   7
  //   NOT
  //   8
  //   NOT
  //   9
  //   SHF
  //   A
  //   SHF
  //   B
  //   JPZ
  //   C
  //   JPO
  //   D
  //   GO
  //   E
  //   STR
  //   F
  //   Instruction Set
  //   0
  //   000
  //   AC <= X
  //   1
  //   000
  //   0
  //   001
  //   1
  //   001
  //   010
  //   0
  //   1
  //   010
  //   0
  //   011
  //   1
  //   011
  //   0
  //   100
  //   100
  //   1
  //   0
  //   101
  //   1
  //   101
  //   110
  //   0
  //   1
  //   110
  //   PC <= X
  //   111
  //   0
  //   1
  //   111
  //   AC <= M(X)
  //   AC <= AC+X
  //   AC <= AC+M(X)
  //   AC <= AC-X
  //   AC <= AC-M(X)
  //   AC <= AC OR X
  //   AC <= AC OR M(X)
  //   AC <= NOT X
  //   AC <= NOT M( X)
  //   AC <= AC << Q
  //   AC <= AC >> Q
  //   PC <= X SE FLAG Z
  //   PC <= X SE FLAG O
  //   M(X) <= AC 
endmodule

module Add_1 (
  input  A,
  input  B,
  input  C,
  output S,
  output Vai_1
);

  wire and_1_out, and_2_out, or_1_out, xor_1_out;

  xor xor_1 (xor_1_out, B, C);
  or or_1 (or_1_out, B, C);
  xor xor_2 (S, A, xor_1_out);
  and and_1 (and_1_out, or_1_out, A);
  and and_2 (and_2_out, C, B);
  or or_2 (Vai_1, and_1_out, and_2_out);
endmodule

module Add_4 (
  input  [3:0] B,
  input  [3:0] A,
  output Overflow,
  output [3:0] S
);

  wire add_1_2_vai_1, add_1_3_vai_1, add_1_4_vai_1;

  Add_1 add_1_1 (.S(S[3]), .Vai_1(Overflow), .A(A[3]), .B(B[3]), .C(add_1_2_vai_1));
  Add_1 add_1_2 (.S(S[2]), .Vai_1(add_1_2_vai_1), .A(A[2]), .B(B[2]), .C(add_1_4_vai_1));
  Add_1 add_1_3 (.S(S[0]), .Vai_1(add_1_3_vai_1), .A(A[0]), .B(B[0]), .C(1'b0));
  Add_1 add_1_4 (.S(S[1]), .Vai_1(add_1_4_vai_1), .A(A[1]), .B(B[1]), .C(add_1_3_vai_1));
endmodule

module Sub_1 (
  input  A,
  input  B,
  input  C,
  output S,
  output Vai_1
);

  wire and_1_out, and_2_out, or_1_out, xor_1_out;

  xor xor_1 (xor_1_out, C, B);
  or or_1 (or_1_out, C, B);
  xor xor_2 (S, xor_1_out, A);
  and and_1 (and_1_out, or_1_out, ~A);  // AND_Gate
  and and_2 (and_2_out, C, B);
  or or_2 (Vai_1, and_1_out, and_2_out);
endmodule

module Sub_4 (
  input  [3:0] B,
  input  [3:0] A,
  output Overflow,
  output [3:0] S
);

  wire sub_1_2_vai_1, sub_1_3_vai_1, sub_1_4_vai_1;

  Sub_1 sub_1_1 (.S(S[3]), .Vai_1(Overflow), .A(A[3]), .B(B[3]), .C(sub_1_2_vai_1));
  Sub_1 sub_1_2 (.S(S[2]), .Vai_1(sub_1_2_vai_1), .A(A[2]), .B(B[2]), .C(sub_1_4_vai_1));
  Sub_1 sub_1_3 (.S(S[0]), .Vai_1(sub_1_3_vai_1), .A(A[0]), .B(B[0]), .C(1'b0));
  Sub_1 sub_1_4 (.S(S[1]), .Vai_1(sub_1_4_vai_1), .A(A[1]), .B(B[1]), .C(sub_1_3_vai_1));
endmodule

module Rot_Esq (
  input  [1:0] xy,
  input  [3:0] abcd,
  output [3:0] ABCD_2
);

  wire and_1_out, and_2_out, and_3_out, and_4_out, and_5_out, and_6_out, and_7_out, and_8_out, and_9_out;

  and and_1 (and_1_out, ~xy[1], ~xy[0], abcd[3]);  // AND_Gate
  and and_2 (and_2_out, ~xy[1], xy[0], abcd[2]);  // AND_Gate
  and and_3 (and_3_out, xy[1], ~xy[0], abcd[1]);  // AND_Gate
  and and_4 (and_4_out, xy[1], xy[0], abcd[0]);
  and and_5 (and_5_out, ~xy[1], ~xy[0], abcd[2]);  // AND_Gate
  and and_6 (and_6_out, ~xy[1], xy[0], abcd[1]);  // AND_Gate
  and and_7 (and_7_out, xy[1], ~xy[0], abcd[0]);  // AND_Gate
  and and_8 (and_8_out, ~xy[1], ~xy[0], abcd[1]);  // AND_Gate
  and and_9 (and_9_out, ~xy[1], xy[0], abcd[0]);  // AND_Gate
  and and_10 (ABCD_2[0], ~xy[1], ~xy[0], abcd[0]);  // AND_Gate
  or or_1 (ABCD_2[3], and_1_out, and_2_out, and_3_out, and_4_out);
  or or_2 (ABCD_2[2], and_5_out, and_6_out, and_7_out);
  or or_3 (ABCD_2[1], and_8_out, and_9_out);
endmodule

module Rot_Dir (
  input  [3:0] abcd,
  input  [1:0] xy,
  output [3:0] ABCD_2
);

  wire and_1_out, and_2_out, and_3_out, and_4_out, and_5_out, and_6_out, and_7_out, and_8_out, and_9_out;

  and and_1 (and_1_out, ~xy[1], ~xy[0], abcd[0]);  // AND_Gate
  and and_2 (and_2_out, ~xy[1], xy[0], abcd[1]);  // AND_Gate
  and and_3 (and_3_out, xy[1], ~xy[0], abcd[2]);  // AND_Gate
  and and_4 (and_4_out, xy[1], xy[0], abcd[3]);
  and and_5 (and_5_out, ~xy[1], ~xy[0], abcd[1]);  // AND_Gate
  and and_6 (and_6_out, ~xy[1], xy[0], abcd[2]);  // AND_Gate
  and and_7 (and_7_out, xy[1], ~xy[0], abcd[3]);  // AND_Gate
  and and_8 (and_8_out, ~xy[1], ~xy[0], abcd[2]);  // AND_Gate
  and and_9 (and_9_out, ~xy[1], xy[0], abcd[3]);  // AND_Gate
  and and_10 (ABCD_2[3], ~xy[1], ~xy[0], abcd[3]);  // AND_Gate
  or or_1 (ABCD_2[0], and_1_out, and_2_out, and_3_out, and_4_out);
  or or_2 (ABCD_2[1], and_5_out, and_6_out, and_7_out);
  or or_3 (ABCD_2[2], and_8_out, and_9_out);
endmodule

module Buffer (
  input  [3:0] E,
  input  in_2,
  output [3:0] S
);

  assign S[3] = in_2 ? E[3] : 1'bz;  // Controlled_Buffer controlled_buffer_1
  assign S[2] = in_2 ? E[2] : 1'bz;  // Controlled_Buffer controlled_buffer_2
  assign S[1] = in_2 ? E[1] : 1'bz;  // Controlled_Buffer controlled_buffer_3
  assign S[0] = in_2 ? E[0] : 1'bz;  // Controlled_Buffer controlled_buffer_4
endmodule

module Dec3x8 (
  input  [2:0] in_1,
  output S0,
  output S1,
  output S2,
  output S3,
  output S4,
  output S5,
  output S6,
  output S7
);

  wire not_1_out, not_2_out, not_3_out, not_4_out, not_5_out, not_6_out, not_7_out, not_8_out, not_9_out,
       not_10_out, not_11_out, not_12_out;

  not not_1 (not_1_out, in_1[2]);
  not not_2 (not_2_out, in_1[1]);
  not not_3 (not_3_out, in_1[0]);
  not not_4 (not_4_out, in_1[2]);
  not not_5 (not_5_out, in_1[1]);
  not not_6 (not_6_out, in_1[2]);
  not not_7 (not_7_out, in_1[0]);
  not not_8 (not_8_out, in_1[2]);
  not not_9 (not_9_out, in_1[1]);
  not not_10 (not_10_out, in_1[0]);
  not not_11 (not_11_out, in_1[1]);
  not not_12 (not_12_out, in_1[0]);
  and and_1 (S0, not_1_out, not_2_out, not_3_out);
  and and_2 (S1, not_4_out, not_5_out, in_1[0]);
  and and_3 (S2, not_6_out, in_1[1], not_7_out);
  and and_4 (S3, not_8_out, in_1[1], in_1[0]);
  and and_5 (S4, in_1[2], not_9_out, not_10_out);
  and and_6 (S5, in_1[2], not_11_out, in_1[0]);
  and and_7 (S6, in_1[2], in_1[1], not_12_out);
  and and_8 (S7, in_1[2], in_1[1], in_1[0]);
endmodule

module Or_4 (
  input  [3:0] B,
  input  [3:0] A,
  output [3:0] S
);

  or or_1 (S[3], A[3], B[3]);
  or or_2 (S[2], A[2], B[2]);
  or or_3 (S[1], A[1], B[1]);
  or or_4 (S[0], A[0], B[0]);
endmodule

module Not_4 (
  input  [3:0] E,
  output [3:0] S
);

  not not_1 (S[3], E[3]);
  not not_2 (S[1], E[1]);
  not not_3 (S[2], E[2]);
  not not_4 (S[0], E[0]);
endmodule

module ULA (
  input  D,
  input  [3:0] B,
  input  [3:0] A,
  input  [2:0] in_4,
  output Overflow,
  output [3:0] S,
  output zero
);

  wire add_4_1_overflow, and_1_out, and_2_out, dec3x8_1_s0, dec3x8_1_s1, dec3x8_1_s2, dec3x8_1_s3,
       dec3x8_1_s4, dec3x8_1_s5, dec3x8_1_s6, dec3x8_1_s7, not_1_out, sub_4_1_overflow;
  wire [3:0] add_4_1_s, buffer_6_s, not_4_1_s, or_4_1_s, rot_dir_1_abcd_2, rot_esq_1_abcd_2, sub_4_1_s;

  or or_1 (Overflow, and_1_out, and_2_out);
  and and_1 (and_1_out, add_4_1_overflow, dec3x8_1_s1);
  and and_2 (and_2_out, sub_4_1_overflow, dec3x8_1_s2);
  Buffer buffer_1 (.E(B), .in_2(dec3x8_1_s0), .S(S));
  Dec3x8 dec3x8_1 (
    .S0(dec3x8_1_s0), .S1(dec3x8_1_s1), .S2(dec3x8_1_s2), .S3(dec3x8_1_s3), .S4(dec3x8_1_s4),
    .S5(dec3x8_1_s5), .S6(dec3x8_1_s6), .S7(dec3x8_1_s7), .in_1(in_4));
  Add_4 add_4_1 (.A(A), .B(B), .S(add_4_1_s), .Overflow(add_4_1_overflow));
  Buffer buffer_2 (.E(add_4_1_s), .in_2(dec3x8_1_s1), .S(S));
  Or_4 or_4_1 (.A(A), .B(B), .S(or_4_1_s));
  Sub_4 sub_4_1 (.A(A), .B(B), .S(sub_4_1_s), .Overflow(sub_4_1_overflow));
  Buffer buffer_3 (.E(sub_4_1_s), .in_2(dec3x8_1_s2), .S(S));
  nor nor_1 (zero, S[0], S[1], S[2], S[3], dec3x8_1_s6, dec3x8_1_s7);
  Not_4 not_4_1 (.E(B), .S(not_4_1_s));
  Buffer buffer_4 (.E(or_4_1_s), .in_2(dec3x8_1_s3), .S(S));
  Buffer buffer_5 (.E(not_4_1_s), .in_2(dec3x8_1_s4), .S(S));
  // Probe on S
  not not_1 (not_1_out, D);
  Rot_Esq rot_esq_1 (.abcd(A), .xy(B[1:0]), .ABCD_2(rot_esq_1_abcd_2));
  Rot_Dir rot_dir_1 (.abcd(A), .xy(B[1:0]), .ABCD_2(rot_dir_1_abcd_2));
  Buffer buffer_6 (.E(rot_esq_1_abcd_2), .in_2(not_1_out), .S(buffer_6_s));
  Buffer buffer_7 (.E(rot_dir_1_abcd_2), .in_2(D), .S(buffer_6_s));
  Buffer buffer_8 (.E(buffer_6_s), .in_2(dec3x8_1_s5), .S(S));
endmodule

module AC (
  input  Clock,
  input  [3:0] E,
  output [3:0] out_3
);

  D_Flip_Flop D3 (.clk(Clock), .D(E[3]), .Q(out_3[3]));  // open: Qn, preset, en, reset
  D_Flip_Flop D2 (.clk(Clock), .D(E[2]), .Q(out_3[2]));  // open: Qn, preset, en, reset
  D_Flip_Flop D1 (.clk(Clock), .D(E[1]), .Q(out_3[1]));  // open: Qn, preset, en, reset
  D_Flip_Flop D0 (.clk(Clock), .D(E[0]), .Q(out_3[0]));  // open: Qn, preset, en, reset
endmodule

module MUX (
  input  [3:0] E,
  input  [3:0] D,
  input  C,
  output [3:0] S
);

  wire not_1_out;

  Buffer buffer_1 (.E(E), .in_2(not_1_out), .S(S));
  not not_1 (not_1_out, C);
  Buffer buffer_2 (.E(D), .in_2(C), .S(S));
endmodule
